// Logisim project Monocycle-processor.circ as structural Verilog: 8 circuits, main circuit main
// ALU
module main (
);

  wire alu_1_zero, ALUSrc, and_1_out, Branch, CLK, control_1_regwrite, MemToReg, MemWrite, not_1_out, RegDist;
  wire [1:0] ALUOp;
  wire [2:0] alucontrol_1_select;
  wire [4:0] multiplexer_1_out;
  wire [31:0] adder_1_out, adder_2_out, Address_Memory_out_2, alu_1_o, Data_Memory_readed_data,
       multiplexer_2_out, multiplexer_3_out, pc_1_next_address, registers_1_read_data_1,
       registers_1_read_data_2, shifter_1_out, SignExtend, WriteData;

  Clock clock_1 (.out(CLK));
  PC pc_1 (.Address_Input(multiplexer_3_out), .CLK(CLK), .Next_Address(pc_1_next_address));
  // Probe on pc_1_next_address
  Adder #(.width(32)) adder_1 (.a(pc_1_next_address), .b(32'h4), .out(adder_1_out));  // open: cin, cout
  // Probe on Address_Memory_out_2
  Address_Memory Address_Memory (.Instruction_Address(pc_1_next_address), .out_2(Address_Memory_out_2));
  // Probe on Address_Memory_out_2[15:0]
  Control control_1 (
    .Instruction(Address_Memory_out_2[31:26]), .RegDst(RegDist), .Branch(Branch), .MemToReg(MemToReg),
    .ALUOp(ALUOp), .MemWrite(MemWrite), .ALUSrc(ALUSrc), .RegWrite(control_1_regwrite));
  Multiplexer #(.width(5), .enable("false")) multiplexer_1 (
    .in0(Address_Memory_out_2[20:16]), .in1(Address_Memory_out_2[15:11]), .out(multiplexer_1_out),
    .sel(RegDist));
  assign SignExtend = {{16{Address_Memory_out_2[15]}}, Address_Memory_out_2[15:0]};  // Bit_Extender bit_extender_1
  // Probe on SignExtend
  Registers registers_1 (
    .Read_Register_1(Address_Memory_out_2[25:21]), .Read_Register_2(Address_Memory_out_2[20:16]),
    .Write_Register(multiplexer_1_out), .Write_Data(WriteData), .Write_Enable(control_1_regwrite), .CLK(CLK),
    .Read_Data_1(registers_1_read_data_1), .Read_data_2(registers_1_read_data_2));
  Multiplexer #(.width(32), .enable("false")) multiplexer_2 (
    .in0(registers_1_read_data_2), .in1(SignExtend), .out(multiplexer_2_out), .sel(ALUSrc));
  ALUControl alucontrol_1 (.ALUOp(ALUOp), .Instruction(Address_Memory_out_2[5:0]), .Select(alucontrol_1_select));
  ALU alu_1 (
    .X(registers_1_read_data_1), .Y(multiplexer_2_out), .ALUSelect(alucontrol_1_select), .O(alu_1_o),
    .Zero(alu_1_zero));
  Shifter #(.width(32)) shifter_1 (.in(SignExtend), .\dist (5'b00010), .out(shifter_1_out));
  Adder #(.width(32)) adder_2 (.a(adder_1_out), .b(shifter_1_out), .out(adder_2_out));  // open: cin, cout
  Data_Memory Data_Memory (
    .Memory_Address(alu_1_o), .Data(registers_1_read_data_2), .MemWrite(MemWrite), .CLK(CLK),
    .Readed_Data(Data_Memory_readed_data));
  Multiplexer #(.width(32), .enable("false")) multiplexer_3 (
    .in0(adder_1_out), .in1(adder_2_out), .out(multiplexer_3_out), .sel(and_1_out));
  and and_1 (and_1_out, Branch, alu_1_zero);
  not not_1 (not_1_out, MemToReg);
  Multiplexer #(.width(32), .enable("false")) multiplexer_4 (
    .in0(Data_Memory_readed_data), .in1(alu_1_o), .out(WriteData), .sel(not_1_out));
endmodule

module PC (
  input  [31:0] Address_Input,
  input  CLK,
  output [31:0] Next_Address
);

  Counter #(.width(32), .max('hffffffff)) counter_1 (
    .load(1'b1), .D(Address_Input), .count(1'b0), .Q(Next_Address), .clk(CLK));  // open: carry, clr
endmodule

// AM
module Address_Memory (
  input  [31:0] Instruction_Address,
  output [31:0] out_2
);

  wire [31:0] shifter_1_out;

  Shifter #(.width(32), .shift("lr")) shifter_1 (.in(Instruction_Address), .\dist (5'b00010), .out(shifter_1_out));
  ROM #(.addrWidth(24), .dataWidth(32)) rom_1 (.addr(shifter_1_out[23:0]), .data(out_2), .sel(1'b1));

  // Notes on the sheet:
  //   contents of rom_1 (hex, n*v repeats v):
  //   23bdffec afa80000 afa90004 afaa0008 afab000c afac0010 20082000 2009201c 8d2a0000 2001d8f1 102a0010
  //   21290004 200c0001 8d0a0000 8d2b0000 2001d8f1 102a000a 2001d8f1 102b0008 20010001 142c0001 ad0b0000
  //   21080004 21290004 2001ffff 71816002 1000fff2 8fa80000 8fa90004 8faa0008 8fab000c 8fac0010 23bd0014
  //   2402000a c
endmodule

// DM
module Data_Memory (
  input  [31:0] Memory_Address,
  input  [31:0] Data,
  input  MemWrite,
  input  CLK,
  output [31:0] Readed_Data
);

  wire [31:0] shifter_1_out;

  Shifter #(.width(32), .shift("lr")) shifter_1 (.in(Memory_Address), .\dist (5'b00010), .out(shifter_1_out));
  RAM #(.addrWidth(24), .dataWidth(32), .bus("separate")) ram_1 (
    .addr(shifter_1_out[23:0]), .din(Data), .data(Readed_Data), .str(MemWrite), .sel(1'b1), .clk(CLK),
    .ld(1'b1), .clr(1'b0));
endmodule

module Registers (
  input  Write_Enable,
  input  [4:0] Read_Register_1,
  input  [4:0] Read_Register_2,
  input  [4:0] Write_Register,
  input  [31:0] Write_Data,
  input  CLK,
  output [31:0] Read_Data_1,
  output [31:0] Read_data_2
);

  wire decoder_1_out0, decoder_1_out1, decoder_1_out2, decoder_1_out3, decoder_1_out4, decoder_1_out5,
       decoder_1_out6, decoder_1_out7, decoder_1_out8, decoder_1_out9, decoder_1_out10, decoder_1_out11,
       decoder_1_out12, decoder_1_out13, decoder_1_out14, decoder_1_out15, decoder_1_out16, decoder_1_out17,
       decoder_1_out18, decoder_1_out19, decoder_1_out20, decoder_1_out21, decoder_1_out22, decoder_1_out23,
       decoder_1_out24, decoder_1_out25, decoder_1_out26, decoder_1_out27, decoder_1_out28, decoder_1_out29,
       decoder_1_out30, decoder_1_out31;
  wire [31:0] register_1_q, register_2_q, register_3_q, register_4_q, register_5_q, register_6_q,
       register_7_q, register_8_q, register_9_q, register_10_q, register_11_q, register_12_q, register_13_q,
       register_14_q, register_15_q, register_16_q, register_17_q, register_18_q, register_19_q,
       register_20_q, register_21_q, register_22_q, register_23_q, register_24_q, register_25_q,
       register_26_q, register_27_q, register_28_q, register_29_q, register_30_q, register_31_q,
       register_32_q;

  Decoder #(.select(5)) decoder_1 (
    .out0(decoder_1_out0), .out1(decoder_1_out1), .out2(decoder_1_out2), .out3(decoder_1_out3),
    .out4(decoder_1_out4), .out5(decoder_1_out5), .out6(decoder_1_out6), .out7(decoder_1_out7),
    .out8(decoder_1_out8), .out9(decoder_1_out9), .out10(decoder_1_out10), .out11(decoder_1_out11),
    .out12(decoder_1_out12), .out13(decoder_1_out13), .out14(decoder_1_out14), .out15(decoder_1_out15),
    .out16(decoder_1_out16), .out17(decoder_1_out17), .out18(decoder_1_out18), .out19(decoder_1_out19),
    .out20(decoder_1_out20), .out21(decoder_1_out21), .out22(decoder_1_out22), .out23(decoder_1_out23),
    .out24(decoder_1_out24), .out25(decoder_1_out25), .out26(decoder_1_out26), .out27(decoder_1_out27),
    .out28(decoder_1_out28), .out29(decoder_1_out29), .out30(decoder_1_out30), .out31(decoder_1_out31),
    .sel(Write_Register), .en(Write_Enable));
  Register #(.width(32)) register_1 (.D(Write_Data), .en(decoder_1_out0), .Q(register_1_q), .clk(CLK));  // open: clr
  Register #(.width(32)) register_2 (.D(Write_Data), .en(decoder_1_out1), .Q(register_2_q), .clk(CLK));  // open: clr
  Register #(.width(32)) register_3 (.D(Write_Data), .en(decoder_1_out2), .Q(register_3_q), .clk(CLK));  // open: clr
  Register #(.width(32)) register_4 (.D(Write_Data), .en(decoder_1_out3), .Q(register_4_q), .clk(CLK));  // open: clr
  Register #(.width(32)) register_5 (.D(Write_Data), .en(decoder_1_out4), .Q(register_5_q), .clk(CLK));  // open: clr
  Register #(.width(32)) register_6 (.D(Write_Data), .en(decoder_1_out5), .Q(register_6_q), .clk(CLK));  // open: clr
  Register #(.width(32)) register_7 (.D(Write_Data), .en(decoder_1_out6), .Q(register_7_q), .clk(CLK));  // open: clr
  Register #(.width(32)) register_8 (.D(Write_Data), .en(decoder_1_out7), .Q(register_8_q), .clk(CLK));  // open: clr
  Register #(.width(32)) register_9 (.D(Write_Data), .en(decoder_1_out8), .Q(register_9_q), .clk(CLK));  // open: clr
  Register #(.width(32)) register_10 (.D(Write_Data), .en(decoder_1_out9), .Q(register_10_q), .clk(CLK));  // open: clr
  Register #(.width(32)) register_11 (.D(Write_Data), .en(decoder_1_out10), .Q(register_11_q), .clk(CLK));  // open: clr
  Register #(.width(32)) register_12 (.D(Write_Data), .en(decoder_1_out11), .Q(register_12_q), .clk(CLK));  // open: clr
  Register #(.width(32)) register_13 (.D(Write_Data), .en(decoder_1_out12), .Q(register_13_q), .clk(CLK));  // open: clr
  Register #(.width(32)) register_14 (.D(Write_Data), .en(decoder_1_out13), .Q(register_14_q), .clk(CLK));  // open: clr
  Register #(.width(32)) register_15 (.D(Write_Data), .en(decoder_1_out14), .Q(register_15_q), .clk(CLK));  // open: clr
  Register #(.width(32)) register_16 (.D(Write_Data), .en(decoder_1_out15), .Q(register_16_q), .clk(CLK));  // open: clr
  Register #(.width(32)) register_17 (.D(Write_Data), .en(decoder_1_out16), .Q(register_17_q), .clk(CLK));  // open: clr
  Register #(.width(32)) register_18 (.D(Write_Data), .en(decoder_1_out17), .Q(register_18_q), .clk(CLK));  // open: clr
  Register #(.width(32)) register_19 (.D(Write_Data), .en(decoder_1_out18), .Q(register_19_q), .clk(CLK));  // open: clr
  Register #(.width(32)) register_20 (.D(Write_Data), .en(decoder_1_out19), .Q(register_20_q), .clk(CLK));  // open: clr
  Register #(.width(32)) register_21 (.D(Write_Data), .en(decoder_1_out20), .Q(register_21_q), .clk(CLK));  // open: clr
  Register #(.width(32)) register_22 (.D(Write_Data), .en(decoder_1_out21), .Q(register_22_q), .clk(CLK));  // open: clr
  Register #(.width(32)) register_23 (.D(Write_Data), .en(decoder_1_out22), .Q(register_23_q), .clk(CLK));  // open: clr
  Register #(.width(32)) register_24 (.D(Write_Data), .en(decoder_1_out23), .Q(register_24_q), .clk(CLK));  // open: clr
  Register #(.width(32)) register_25 (.D(Write_Data), .en(decoder_1_out24), .Q(register_25_q), .clk(CLK));  // open: clr
  Register #(.width(32)) register_26 (.D(Write_Data), .en(decoder_1_out25), .Q(register_26_q), .clk(CLK));  // open: clr
  Register #(.width(32)) register_27 (.D(Write_Data), .en(decoder_1_out26), .Q(register_27_q), .clk(CLK));  // open: clr
  Register #(.width(32)) register_28 (.D(Write_Data), .en(decoder_1_out27), .Q(register_28_q), .clk(CLK));  // open: clr
  Register #(.width(32)) register_29 (.D(Write_Data), .en(decoder_1_out28), .Q(register_29_q), .clk(CLK));  // open: clr
  Register #(.width(32)) register_30 (.D(Write_Data), .en(decoder_1_out29), .Q(register_30_q), .clk(CLK));  // open: clr
  Register #(.width(32)) register_31 (.D(Write_Data), .en(decoder_1_out30), .Q(register_31_q), .clk(CLK));  // open: clr
  Register #(.width(32)) register_32 (.D(Write_Data), .en(decoder_1_out31), .Q(register_32_q), .clk(CLK));  // open: clr
  Multiplexer #(.select(5), .width(32), .enable("false")) multiplexer_1 (
    .in0(register_1_q), .in1(register_2_q), .in2(register_3_q), .in3(register_4_q), .in4(register_5_q),
    .in5(register_6_q), .in6(register_7_q), .in7(register_8_q), .in8(register_9_q), .in9(register_10_q),
    .in10(register_11_q), .in11(register_12_q), .in12(register_13_q), .in13(register_14_q),
    .in14(register_15_q), .in15(register_16_q), .in16(register_17_q), .in17(register_18_q),
    .in18(register_19_q), .in19(register_20_q), .in20(register_21_q), .in21(register_22_q),
    .in22(register_23_q), .in23(register_24_q), .in24(register_25_q), .in25(register_26_q),
    .in26(register_27_q), .in27(register_28_q), .in28(register_29_q), .in29(register_30_q),
    .in30(register_31_q), .in31(register_32_q), .out(Read_Data_1), .sel(Read_Register_1));
  Multiplexer #(.select(5), .width(32), .enable("false")) multiplexer_2 (
    .in0(register_1_q), .in1(register_2_q), .in2(register_3_q), .in3(register_4_q), .in4(register_5_q),
    .in5(register_6_q), .in6(register_7_q), .in7(register_8_q), .in8(register_9_q), .in9(register_10_q),
    .in10(register_11_q), .in11(register_12_q), .in12(register_13_q), .in13(register_14_q),
    .in14(register_15_q), .in15(register_16_q), .in16(register_17_q), .in17(register_18_q),
    .in18(register_19_q), .in19(register_20_q), .in20(register_21_q), .in21(register_22_q),
    .in22(register_23_q), .in23(register_24_q), .in24(register_25_q), .in25(register_26_q),
    .in26(register_27_q), .in27(register_28_q), .in28(register_29_q), .in29(register_30_q),
    .in30(register_31_q), .in31(register_32_q), .out(Read_data_2), .sel(Read_Register_2));
endmodule

module Control (
  input  [5:0] Instruction,
  output RegDst,
  output Branch,
  output MemToReg,
  output [1:0] ALUOp,
  output MemWrite,
  output ALUSrc,
  output RegWrite
);

  // Probe on {RegDst, Branch, MemToReg, ALUOp, MemWrite, ALUSrc, RegWrite}
  ROM #(.addrWidth(6)) rom_1 (
    .addr(Instruction), .data({RegDst, Branch, MemToReg, ALUOp, MemWrite, ALUSrc, RegWrite}), .sel(1'b1));

  // Notes on the sheet:
  //   contents of rom_1 (hex, n*v repeats v):
  //   99 0 0 0 40 48 0 0 1b 26*0 13 7*0 16
endmodule

module ALU (
  input  [31:0] X,
  input  [31:0] Y,
  input  [2:0] ALUSelect,
  output [31:0] O,
  output Zero
);

  wire and_1_out, comparator_1_lt, not_1_out, Zero_t;
  wire [31:0] adder_1_out, and_2_out, bit_extender_1_out, multiplier_1_out, nor_1_out, or_1_out,
       subtractor_1_out;

  Multiplexer #(.enable("false")) multiplexer_1 (.in0(Zero_t), .in1(not_1_out), .out(Zero), .sel(and_1_out));
  not not_1 (not_1_out, Zero_t);
  and and_1 (and_1_out, ALUSelect[2], ~ALUSelect[1], ALUSelect[0]);  // AND_Gate
  assign nor_1_out = ~(X | Y);  // NOR_Gate nor_1, 32 bits wide
  Adder #(.width(32)) adder_1 (.a(X), .b(Y), .out(adder_1_out));  // open: cin, cout
  Subtractor #(.width(32)) subtractor_1 (.a(X), .b(Y), .out(subtractor_1_out));  // open: bin, bout
  Comparator #(.width(32)) comparator_1 (.a(X), .b(Y), .eq(Zero_t), .lt(comparator_1_lt));  // open: gt
  Multiplier #(.width(32)) multiplier_1 (.a(X), .b(Y), .out(multiplier_1_out));  // open: cin, cout
  assign and_2_out = X & Y;  // AND_Gate and_2, 32 bits wide
  assign or_1_out = X | Y;  // OR_Gate or_1, 32 bits wide
  assign bit_extender_1_out = {{31{1'b0}}, comparator_1_lt};  // Bit_Extender bit_extender_1
  Multiplexer #(.select(3), .width(32), .enable("false")) multiplexer_2 (
    .in0(nor_1_out), .in1(adder_1_out), .in2(subtractor_1_out), .in3(bit_extender_1_out),
    .in4(multiplier_1_out), .in5({32{1'b0}}), .in6(and_2_out), .in7(or_1_out), .out(O), .sel(ALUSelect));

  // Other names for the same wires on the sheet: OUT[31:0] = O; Select[2:0] = ALUSelect
endmodule

module ALUControl (
  input  [1:0] ALUOp,
  input  [5:0] Instruction,
  output [2:0] Select
);

  wire [2:0] Select_t;

  // Probe on Instruction
  ROM #(.addrWidth(6), .dataWidth(3)) rom_1 (.addr(Instruction), .data(Select_t), .sel(1'b1));
  Multiplexer #(.select(2), .width(3), .enable("false")) multiplexer_1 (
    .in0(3'b011), .in1(3'b101), .in2(3'b001), .in3(Select_t), .out(Select), .sel(ALUOp));

  // Other names for the same wires on the sheet: Instr[5:0] = Instruction

  // Notes on the sheet:
  //   contents of rom_1 (hex, n*v repeats v):
  //   24*0 4 7*0 1 0 2 0 7 6 4*0 3
endmodule
